// Logisim project CKT_B1.circ as structural Verilog: 2 circuits, main circuit main
module main (
  input  S,
  input  H,
  input  C,
  input  T,
  output X
);

  wire and_1_out;

  and and_1 (and_1_out, H, C);
  or or_1 (X, and_1_out, S);
endmodule

module unsimplified (
  input  S,
  input  H,
  input  C,
  input  T,
  output X
);

  wire and_1_out, and_2_out, not_1_out;

  and and_1 (and_1_out, H, C);
  not not_1 (not_1_out, T);
  and and_2 (and_2_out, and_1_out, not_1_out);
  or or_1 (X, and_2_out, S);
endmodule
