// Logisim project CKT_B1_CORRECTED.circ as structural Verilog: 1 circuit, main circuit main
module main (
  input  S,
  input  H,
  input  C,
  input  T,
  output X
);

  wire and_1_out, and_2_out, and_3_out, and_4_out, and_5_out, and_6_out, and_7_out, and_8_out, and_9_out,
       not_1_out, not_2_out, not_3_out, not_4_out, not_5_out, not_6_out, not_7_out, not_8_out, or_1_out,
       or_2_out;

  not not_1 (not_1_out, S);
  and and_1 (and_1_out, not_1_out, H);
  and and_2 (and_2_out, C, not_2_out);
  not not_2 (not_2_out, T);
  and and_3 (and_3_out, S, not_3_out);
  not not_3 (not_3_out, H);
  not not_4 (not_4_out, C);
  and and_4 (and_4_out, S, not_5_out);
  not not_5 (not_5_out, H);
  not not_6 (not_6_out, T);
  and and_5 (and_5_out, S, not_7_out);
  not not_7 (not_7_out, C);
  not not_8 (not_8_out, T);
  and and_6 (and_6_out, and_1_out, and_2_out);
  and and_7 (and_7_out, and_3_out, not_4_out);
  and and_8 (and_8_out, and_4_out, not_6_out);
  and and_9 (and_9_out, and_5_out, not_8_out);
  or or_1 (or_1_out, and_6_out, and_7_out);
  or or_2 (or_2_out, and_8_out, and_9_out);
  or or_3 (X, or_1_out, or_2_out);
endmodule
