// Logisim project B1.circ as structural Verilog: 5 circuits, main circuit main
module main (
  input  I0,
  input  I1,
  input  I2,
  input  I3,
  input  I4,
  input  I5,
  input  I6,
  input  I7,
  input  E,
  input  S0,
  input  S1,
  input  S2,
  output A0,
  output A1,
  output A2
);

  wire and_1_out, and_2_out, and_3_out, and_4_out, and_5_out, and_6_out, and_7_out, and_8_out, and_9_out,
       and_10_out, and_11_out, and_12_out, and_13_out, and_14_out, and_15_out, and_16_out, and_17_out,
       and_18_out, and_19_out, and_20_out, not_1_out, not_2_out, not_3_out, not_4_out, not_5_out, not_6_out,
       not_7_out, not_8_out, not_9_out, not_10_out, not_11_out, not_12_out, not_13_out, not_14_out,
       not_15_out, not_16_out, not_17_out, not_18_out, not_19_out, not_20_out, not_21_out, not_22_out,
       not_23_out, not_24_out, not_25_out, not_26_out, not_27_out, not_28_out, not_29_out;

  not not_1 (not_1_out, E);
  not not_2 (not_2_out, S0);
  not not_3 (not_3_out, E);
  not not_4 (not_4_out, S1);
  not not_5 (not_5_out, I6);
  not not_6 (not_6_out, E);
  not not_7 (not_7_out, S0);
  not not_8 (not_8_out, S1);
  not not_9 (not_9_out, E);
  not not_10 (not_10_out, S2);
  not not_11 (not_11_out, I4);
  not not_12 (not_12_out, I6);
  not not_13 (not_13_out, E);
  not not_14 (not_14_out, S0);
  not not_15 (not_15_out, S2);
  not not_16 (not_16_out, E);
  not not_17 (not_17_out, S1);
  not not_18 (not_18_out, S2);
  not not_19 (not_19_out, I2);
  not not_20 (not_20_out, I4);
  not not_21 (not_21_out, I6);
  not not_22 (not_22_out, E);
  not not_23 (not_23_out, S0);
  not not_24 (not_24_out, S1);
  not not_25 (not_25_out, S2);
  not not_26 (not_26_out, I4);
  not not_27 (not_27_out, I5);
  not not_28 (not_28_out, I4);
  not not_29 (not_29_out, I5);
  and and_1 (and_1_out, I7, E);
  and and_2 (and_2_out, I6, E);
  and and_3 (and_3_out, I5, E);
  and and_4 (and_4_out, I4, E);
  and and_5 (and_5_out, I7, S0, S1, S2);
  and and_6 (and_6_out, I7, E);
  and and_7 (and_7_out, I6, not_1_out, not_2_out, S1, S2);
  and and_8 (and_8_out, I5, not_3_out, S0, not_4_out, S2);
  and and_9 (and_9_out, I5, not_5_out, E);
  and and_10 (and_10_out, I4, not_6_out, not_7_out, not_8_out, S2);
  and and_11 (and_11_out, I3, not_9_out, S0, S1, not_10_out);
  and and_12 (and_12_out, I3, not_11_out, not_12_out, E);
  and and_13 (and_13_out, I2, not_13_out, not_14_out, S1, not_15_out);
  and and_14 (and_14_out, I1, not_16_out, S0, not_17_out, not_18_out);
  and and_15 (and_15_out, I1, not_19_out, not_20_out, not_21_out, E);
  and and_16 (and_16_out, I0, not_22_out, not_23_out, not_24_out, not_25_out);
  and and_17 (and_17_out, I7, E);
  and and_18 (and_18_out, I6, E);
  and and_19 (and_19_out, I3, not_26_out, not_27_out, E);
  and and_20 (and_20_out, I2, not_28_out, not_29_out, E);
  or or_1 (A2, and_1_out, and_2_out, and_3_out, and_4_out);
  or or_2 (A0, and_5_out, and_6_out, and_7_out, and_8_out, and_9_out, and_10_out, and_11_out, and_12_out, and_13_out, and_14_out, and_15_out, and_16_out);
  or or_3 (A1, and_17_out, and_18_out, and_19_out, and_20_out);
endmodule

module _83ENC (
  input  D0,
  input  D1,
  input  D2,
  input  D3,
  input  D4,
  input  D5,
  input  D6,
  input  D7,
  input  E,
  input  S0,
  input  S1,
  input  S2,
  output Q0,
  output Q1,
  output Q2
);

  wire and_1_out, and_2_out, and_3_out, and_4_out, and_5_out, and_6_out, and_7_out, and_8_out, and_9_out,
       and_10_out, and_11_out, and_12_out, and_13_out, and_14_out, and_15_out, and_16_out, not_1_out,
       not_2_out, not_3_out, not_4_out, not_5_out, not_6_out, not_7_out, not_8_out, not_9_out, not_10_out,
       not_11_out, not_12_out, not_13_out, not_14_out, not_15_out, not_16_out, not_17_out, not_18_out,
       not_19_out, not_20_out, not_21_out, or_1_out, or_2_out, or_3_out, or_4_out, or_5_out, or_6_out;

  not not_1 (not_1_out, D4);
  and and_1 (and_1_out, not_1_out, not_2_out, D1);
  not not_2 (not_2_out, D2);
  not not_3 (not_3_out, D4);
  and and_2 (and_2_out, not_3_out, D3);
  not not_4 (not_4_out, D5);
  not not_5 (not_5_out, D4);
  or or_1 (or_1_out, D2, D3);
  not not_6 (not_6_out, S2);
  not not_7 (not_7_out, S1);
  not not_8 (not_8_out, S0);
  not not_9 (not_9_out, S2);
  not not_10 (not_10_out, S1);
  not not_11 (not_11_out, S2);
  not not_12 (not_12_out, S0);
  not not_13 (not_13_out, S2);
  not not_14 (not_14_out, S1);
  not not_15 (not_15_out, S0);
  not not_16 (not_16_out, S1);
  not not_17 (not_17_out, S0);
  not not_18 (not_18_out, D6);
  or or_2 (or_2_out, and_1_out, and_2_out, D5);
  not not_19 (not_19_out, E);
  and and_3 (and_3_out, not_4_out, not_5_out, or_1_out);
  or or_3 (or_3_out, and_3_out, D6, D7);
  and and_4 (and_4_out, D0, not_6_out, not_7_out, not_8_out);
  and and_5 (and_5_out, D1, not_9_out, not_10_out, S0);
  and and_6 (and_6_out, D2, not_11_out, S1, not_12_out);
  and and_7 (and_7_out, D3, not_13_out, S1, S0);
  and and_8 (and_8_out, D4, S2, not_14_out, not_15_out);
  and and_9 (and_9_out, D5, S2, not_16_out, S0);
  and and_10 (and_10_out, D6, S2, S1, not_17_out);
  and and_11 (and_11_out, D7, S2, S1, S0);
  and and_12 (and_12_out, not_18_out, or_2_out);
  and and_13 (and_13_out, not_19_out, or_3_out);
  not not_20 (not_20_out, E);
  or or_4 (or_4_out, D4, D5, D6, D7);
  or or_5 (or_5_out, and_4_out, and_5_out, and_6_out, and_7_out, and_8_out, and_9_out, and_10_out, and_11_out);
  not not_21 (not_21_out, E);
  or or_6 (or_6_out, and_12_out, D7);
  assign Q1 = not_19_out ? and_13_out : 1'bz;  // Controlled_Buffer controlled_buffer_1
  and and_14 (and_14_out, not_20_out, or_4_out);
  and and_15 (and_15_out, E, or_5_out);
  assign Q0 = not_19_out ? and_16_out : 1'bz;  // Controlled_Buffer controlled_buffer_2
  and and_16 (and_16_out, not_21_out, or_6_out);
  or or_7 (Q2, and_14_out, and_15_out);
endmodule

module testing (
  input  [7:0] Input,
  input  Toggle,
  input  [2:0] Select,
  output [2:0] Out
);

  _83ENC _83ENC81MUX (
    .D0(Input[0]), .D1(Input[1]), .D2(Input[2]), .D3(Input[3]), .D4(Input[4]), .D5(Input[5]), .D6(Input[6]),
    .D7(Input[7]), .E(Toggle), .S0(Select[0]), .S1(Select[1]), .S2(Select[2]), .Q0(Out[0]), .Q1(Out[1]),
    .Q2(Out[2]));

  // Notes on the sheet:
  //   0: Encoder
  //   1: Multiplexer
endmodule

module _83ENC1 (
  input  I0,
  input  I1,
  input  I2,
  input  I3,
  input  I4,
  input  I5,
  input  I6,
  input  I7,
  output Q0,
  output Q1,
  output Q2
);

  wire and_1_out, and_2_out, and_3_out, and_4_out, not_1_out, not_2_out, not_3_out, not_4_out, not_5_out,
       not_6_out, or_1_out, or_3_out;

  not not_1 (not_1_out, I4);
  not not_2 (not_2_out, I2);
  and and_1 (and_1_out, not_1_out, not_2_out, I1);
  not not_3 (not_3_out, I4);
  and and_2 (and_2_out, not_3_out, I3);
  not not_4 (not_4_out, I5);
  not not_5 (not_5_out, I4);
  or or_1 (or_1_out, I2, I3);
  or or_2 (Q2, I4, I5, I6, I7);
  not not_6 (not_6_out, I6);
  or or_3 (or_3_out, and_1_out, and_2_out, I5);
  and and_3 (and_3_out, not_4_out, not_5_out, or_1_out);
  or or_4 (Q1, and_3_out, I6, I7);
  and and_4 (and_4_out, not_6_out, or_3_out);
  or or_5 (Q0, and_4_out, I7);
endmodule

module _81MUL (
  input  I0,
  input  I1,
  input  I2,
  input  I3,
  input  I4,
  input  I5,
  input  I6,
  input  I7,
  input  S0,
  input  S1,
  input  S2,
  output Q0
);

  wire and_1_out, and_2_out, and_3_out, and_4_out, and_5_out, and_6_out, and_7_out, and_8_out, not_1_out,
       not_2_out, not_3_out, not_4_out, not_5_out, not_6_out, not_7_out, not_8_out, not_9_out, not_10_out,
       not_11_out, not_12_out;

  not not_1 (not_1_out, S2);
  not not_2 (not_2_out, S1);
  not not_3 (not_3_out, S0);
  not not_4 (not_4_out, S2);
  not not_5 (not_5_out, S1);
  not not_6 (not_6_out, S2);
  not not_7 (not_7_out, S0);
  not not_8 (not_8_out, S2);
  not not_9 (not_9_out, S1);
  not not_10 (not_10_out, S0);
  not not_11 (not_11_out, S1);
  not not_12 (not_12_out, S0);
  and and_1 (and_1_out, I0, not_1_out, not_2_out, not_3_out);
  and and_2 (and_2_out, I1, not_4_out, not_5_out, S0);
  and and_3 (and_3_out, I2, not_6_out, S1, not_7_out);
  and and_4 (and_4_out, I3, not_8_out, S1, S0);
  and and_5 (and_5_out, I4, S2, not_9_out, not_10_out);
  and and_6 (and_6_out, I5, S2, not_11_out, S0);
  and and_7 (and_7_out, I6, S2, S1, not_12_out);
  and and_8 (and_8_out, I7, S2, S1, S0);
  or or_1 (Q0, and_1_out, and_2_out, and_3_out, and_4_out, and_5_out, and_6_out, and_7_out, and_8_out);
endmodule
