// Logisim project B2.circ as structural Verilog: 11 circuits, main circuit main
module main (
  input  [7:0] A,
  input  [7:0] B,
  input  in_3,
  input  in_4,
  output Carry_Out,
  output [7:0] Result
);

  ALU ALU (.A(A), .B(B), .LUSelect(in_3), .ALUSelect(in_4), .Carry_Out(Carry_Out), .Result(Result));

  // Notes on the sheet:
  //   ALU Operations
  //   X 0 : A+B
  //   1 1 : Comparator
  //   0 1 : Complement
endmodule

// BCD Adder
module _4_bit_BCDAdder (
  input  Carry_In,
  input  [3:0] A,
  input  [3:0] B,
  output Carry_Out,
  output [3:0] Result
);

  wire _0_carry_out, and_1_out, and_2_out;
  wire [3:0] _0_result;

  _4_bit_Adder _0 (.A(A), .B(B), .Carry_In(Carry_In), .Result(_0_result), .Carry_Out(_0_carry_out));
  _4_bit_Adder _1 (
    .A({1'b0, {2{Carry_Out}}, 1'b0}), .B(_0_result), .Carry_In(1'b0), .Result(Result));  // open: Carry_Out
  and and_1 (and_1_out, _0_result[3], _0_result[2]);
  and and_2 (and_2_out, _0_result[3], _0_result[1]);
  or or_1 (Carry_Out, and_1_out, _0_carry_out, and_2_out);

  // Notes on the sheet:
  //   4-bit BCD Adder
endmodule

// FA
module _1_bit_Adder (
  input  Carry_In,
  input  A,
  input  B,
  output Result,
  output Carry_Out
);

  wire and_1_out, and_2_out, xor_1_out;

  and and_1 (and_1_out, A, B);
  xor xor_1 (xor_1_out, A, B);
  or or_1 (Carry_Out, and_1_out, and_2_out);
  and and_2 (and_2_out, Carry_In, xor_1_out);
  xor xor_2 (Result, Carry_In, xor_1_out);

  // Notes on the sheet:
  //   Full Adder
endmodule

// 4-Bit Adder
module _4_bit_Adder (
  input  Carry_In,
  input  [3:0] A,
  input  [3:0] B,
  output [3:0] Result,
  output Carry_Out
);

  wire _0_carry_out, _1_carry_out, _2_carry_out;

  _1_bit_Adder _0 (.A(A[0]), .B(B[0]), .Result(Result[0]), .Carry_In(Carry_In), .Carry_Out(_0_carry_out));
  _1_bit_Adder _1 (.A(A[1]), .B(B[1]), .Result(Result[1]), .Carry_In(_0_carry_out), .Carry_Out(_1_carry_out));
  _1_bit_Adder _2 (.A(A[2]), .B(B[2]), .Result(Result[2]), .Carry_In(_1_carry_out), .Carry_Out(_2_carry_out));
  _1_bit_Adder _3 (.A(A[3]), .B(B[3]), .Result(Result[3]), .Carry_In(_2_carry_out), .Carry_Out(Carry_Out));

  // Notes on the sheet:
  //   4-bit Adder
endmodule

module _8_bit_BCD_Adder (
  input  [7:0] A,
  input  [7:0] B,
  output [7:0] Result,
  output Carry_Out
);

  wire n4_bit_bcdadder_1_carry_out;

  _4_bit_BCDAdder u_4_bit_bcdadder_1 (
    .A(A[3:0]), .B(B[3:0]), .Carry_Out(n4_bit_bcdadder_1_carry_out), .Result(Result[3:0]), .Carry_In(1'b0));
  _4_bit_BCDAdder u_4_bit_bcdadder_2 (
    .A(A[7:4]), .B(B[7:4]), .Carry_Out(Carry_Out), .Result(Result[7:4]),
    .Carry_In(n4_bit_bcdadder_1_carry_out));

  // Notes on the sheet:
  //   8-bit BCD Adder
endmodule

module AU (
  input  [7:0] A,
  input  [7:0] B,
  output [7:0] BCD_Result,
  output Carry_Out
);

  _8_bit_BCD_Adder _8_bit_BCD_Adder (.A(A), .B(B), .Result(BCD_Result), .Carry_Out(Carry_Out));

  // Notes on the sheet:
  //   Arithmetic Unit
endmodule

module ALU (
  input  [7:0] A,
  input  [7:0] B,
  input  LUSelect,
  input  ALUSelect,
  output Carry_Out,
  output [7:0] Result
);

  wire [7:0] AU_bcd_result, LU_result;

  AU AU (.A(A), .B(B), .BCD_Result(AU_bcd_result), .Carry_Out(Carry_Out));
  LU LU (.A(A), .B(B), .Choose(LUSelect), .Result(LU_result));
  Multiplexer #(.width(8), .enable("false")) multiplexer_1 (
    .in0(AU_bcd_result), .in1(LU_result), .out(Result), .sel(ALUSelect));

  // Notes on the sheet:
  //   ALU
  //   1: 8-bit Comparator
  //   0: 8-bit Complement
  //   0: AU
  //   1: LU
endmodule

module LU (
  input  [7:0] A,
  input  [7:0] B,
  input  Choose,
  output [7:0] Result
);

  wire [7:0] _8_bit_Complement_result;
  wire [7:7] _8_bit_Comparator_result;

  _8_Bit_Complement _8_bit_Complement (.A(A), .Result(_8_bit_Complement_result));
  _8_bit_Comparator _8_bit_Comparator (.A(A), .B(B), .Result(_8_bit_Comparator_result[7]));
  Multiplexer #(.width(8), .enable("false")) multiplexer_1 (
    .in0(_8_bit_Complement_result), .in1({8{_8_bit_Comparator_result[7]}}), .out(Result), .sel(Choose));

  // Notes on the sheet:
  //   Logical Unit
  //   0: 8-bit Complement
  //   1: 8-bit Comparator
endmodule

module _8_Bit_Complement (
  input  [7:0] A,
  output [7:0] Result
);

  not not_1 (Result[0], A[0]);
  not not_2 (Result[1], A[1]);
  not not_3 (Result[2], A[2]);
  not not_4 (Result[3], A[3]);
  not not_5 (Result[4], A[4]);
  not not_6 (Result[5], A[5]);
  not not_7 (Result[6], A[6]);
  not not_8 (Result[7], A[7]);

  // Notes on the sheet:
  //   8-bit Complement
endmodule

module _8_bit_Comparator (
  input  [7:0] A,
  input  [7:0] B,
  output Result
);

  wire and_1_out, xnor_1_out, xnor_2_out, xnor_3_out, xnor_4_out, xnor_5_out, xnor_6_out, xnor_7_out,
       xnor_8_out;

  xnor xnor_1 (xnor_1_out, A[0], B[0]);
  xnor xnor_2 (xnor_2_out, A[1], B[1]);
  xnor xnor_3 (xnor_3_out, A[2], B[2]);
  xnor xnor_4 (xnor_4_out, A[3], B[3]);
  xnor xnor_5 (xnor_5_out, A[4], B[4]);
  xnor xnor_6 (xnor_6_out, A[5], B[5]);
  xnor xnor_7 (xnor_7_out, A[6], B[6]);
  xnor xnor_8 (xnor_8_out, A[7], B[7]);
  and and_1 (and_1_out, xnor_1_out, xnor_2_out, xnor_3_out, xnor_4_out, xnor_5_out, xnor_6_out, xnor_7_out, xnor_8_out);
  assign Result = and_1_out ? and_1_out : 1'bz;  // Controlled_Buffer controlled_buffer_1

  // Notes on the sheet:
  //   8-bit Comparator
endmodule

module sh (
  input  A,
  input  B,
  output C
);


  assign C = A;
endmodule
