// Logisim project 03.circ as structural Verilog
module BIN2XS3 (
  input  B3,
  input  B2,
  input  B1,
  input  B0,
  output E3,
  output E2,
  output E1,
  output E0
);

  wire and_1_out, and_2_out, and_3_out, not_1_out, not_2_out, not_3_out, not_4_out, or_1_out, or_2_out;

  or or_1 (or_1_out, B0, B1);
  not not_1 (not_1_out, B2);
  or or_2 (or_2_out, B0, not_2_out);
  not not_2 (not_2_out, B2);
  not not_3 (not_3_out, B1);
  not not_4 (not_4_out, B0);
  xnor xnor_1 (E1, B1, B0);
  not not_5 (E0, B0);
  and and_1 (and_1_out, B2, or_1_out);
  or or_3 (E3, and_1_out, B3);
  and and_2 (and_2_out, not_1_out, or_2_out);
  and and_3 (and_3_out, B2, not_3_out, not_4_out);
  or or_4 (E2, and_2_out, and_3_out);
endmodule

module XS32BIN (
  input  E3,
  input  E2,
  input  E1,
  input  E0,
  output B3,
  output B2,
  output B1,
  output B0
);

  wire and_1_out, and_3_out, and_4_out, not_1_out, not_2_out, not_3_out, or_1_out, or_2_out;

  and and_1 (and_1_out, E1, E0);
  not not_1 (not_1_out, E2);
  not not_2 (not_2_out, E1);
  or or_1 (or_1_out, not_2_out, not_3_out);
  not not_3 (not_3_out, E0);
  xor xor_1 (B1, E0, E1);
  not not_4 (B0, E0);
  and and_2 (B3, E3, or_2_out);
  or or_2 (or_2_out, E2, and_1_out);
  and and_3 (and_3_out, not_1_out, or_1_out);
  and and_4 (and_4_out, E2, E1, E0);
  or or_3 (B2, and_3_out, and_4_out);
endmodule

module BIN2GRAY (
  input  B3,
  input  B2,
  input  B1,
  input  B0,
  output G3,
  output G2,
  output G1,
  output G0
);

  xor xor_1 (G2, B3, B2);
  xor xor_2 (G1, B2, B1);
  xor xor_3 (G0, B1, B0);

  assign G3 = B3;
endmodule

module GRAY2BIN (
  input  G3,
  input  G2,
  input  G1,
  input  G0,
  output B3,
  output B2,
  output B1,
  output B0
);

  xor xor_1 (B2, G3, G2);
  xor xor_2 (B1, B2, G1);
  xor xor_3 (B0, B1, G0);

  assign B3 = G3;
endmodule
