// Logisim project 05-06.circ as structural Verilog
module _81MUX (
  input  I0,
  input  I1,
  input  I2,
  input  I3,
  input  I4,
  input  I5,
  input  I6,
  input  I7,
  input  S2,
  input  S1,
  input  S0,
  output O
);

  wire and_1_out, and_2_out, and_3_out, and_4_out, and_5_out, and_6_out, and_7_out, and_8_out, not_1_out,
       not_2_out, not_3_out, not_4_out, not_5_out, not_6_out, not_7_out, not_8_out, not_9_out, not_10_out,
       not_11_out, not_12_out;

  not not_1 (not_1_out, S2);
  not not_2 (not_2_out, S1);
  not not_3 (not_3_out, S0);
  not not_4 (not_4_out, S2);
  not not_5 (not_5_out, S1);
  not not_6 (not_6_out, S2);
  not not_7 (not_7_out, S0);
  not not_8 (not_8_out, S2);
  not not_9 (not_9_out, S1);
  not not_10 (not_10_out, S0);
  not not_11 (not_11_out, S1);
  not not_12 (not_12_out, S0);
  and and_1 (and_1_out, I0, not_1_out, not_2_out, not_3_out);
  and and_2 (and_2_out, I1, not_4_out, not_5_out, S0);
  and and_3 (and_3_out, I2, not_6_out, S1, not_7_out);
  and and_4 (and_4_out, I3, not_8_out, S1, S0);
  and and_5 (and_5_out, I4, S2, not_9_out, not_10_out);
  and and_6 (and_6_out, I5, S2, not_11_out, S0);
  and and_7 (and_7_out, I6, S2, S1, not_12_out);
  and and_8 (and_8_out, I7, S2, S1, S0);
  or or_1 (O, and_1_out, and_2_out, and_3_out, and_4_out, and_5_out, and_6_out, and_7_out, and_8_out);
endmodule

module _81DEMUX (
  input  I,
  input  S2,
  input  S1,
  input  S0,
  output O0,
  output O1,
  output O2,
  output O3,
  output O4,
  output O5,
  output O6,
  output O7
);

  wire not_1_out, not_2_out, not_3_out, not_4_out, not_5_out, not_6_out, not_7_out, not_8_out, not_9_out,
       not_10_out, not_11_out, not_12_out;

  not not_1 (not_1_out, S2);
  not not_2 (not_2_out, S1);
  not not_3 (not_3_out, S0);
  not not_4 (not_4_out, S2);
  not not_5 (not_5_out, S1);
  not not_6 (not_6_out, S2);
  not not_7 (not_7_out, S0);
  not not_8 (not_8_out, S2);
  not not_9 (not_9_out, S1);
  not not_10 (not_10_out, S0);
  not not_11 (not_11_out, S1);
  not not_12 (not_12_out, S0);
  and and_1 (O7, I, S2, S1, S0);
  and and_2 (O0, I, not_1_out, not_2_out, not_3_out);
  and and_3 (O1, I, not_4_out, not_5_out, S0);
  and and_4 (O2, I, not_6_out, S1, not_7_out);
  and and_5 (O3, I, not_8_out, S1, S0);
  and and_6 (O4, I, S2, not_9_out, not_10_out);
  and and_7 (O5, I, S2, not_11_out, S0);
  and and_8 (O6, I, S2, S1, not_12_out);
endmodule
