// Logisim project 07.circ as structural Verilog
module OCT2BIN (
  input  O0,
  input  O1,
  input  O2,
  input  O3,
  input  [3:0] in_5,
  input  O4,
  input  O5,
  input  [3:0] in_8,
  input  O6,
  input  O7,
  output B2,
  output B1,
  output B0,
  output [2:0] out_14
);

  wire [1:0] priority_encoder_2_out;
  wire [1:1] priority_encoder_1_out;

  or or_1 (B2, O4, O5, O6, O7);
  or or_2 (B1, O2, O3, O6, O7);
  or or_3 (B0, O1, O3, O5, O7);
  Priority_Encoder #(.select(2)) priority_encoder_1 (
    .in0(in_5[0]), .in1(in_5[1]), .in2(in_5[2]), .in3(in_5[3]), .out({priority_encoder_1_out[1], out_14[0]}));  // open: gs, en_out, en_in
  Priority_Encoder #(.select(2)) priority_encoder_2 (
    .in0(in_8[0]), .in1(in_8[1]), .in2(in_8[2]), .in3(in_8[3]), .out(priority_encoder_2_out));  // open: gs, en_out, en_in
  // OR_Gate or_4 is placed but not wired
  // OR_Gate or_5 is placed but not wired
endmodule

module DEC2BCD (
  input  D0,
  input  D1,
  input  D2,
  input  D3,
  input  D4,
  input  D5,
  input  D6,
  input  D7,
  input  D8,
  input  D9,
  output B3,
  output B2,
  output B1,
  output B0
);

  or or_1 (B3, D8, D9);
  or or_2 (B2, D4, D5, D6, D7);
  or or_3 (B1, D2, D3, D6, D7);
  or or_4 (B0, D1, D3, D5, D7, D9);
endmodule
