// Logisim project 08.circ as structural Verilog
module HA (
  input  A,
  input  B,
  output S,
  output C
);

  xor xor_1 (S, A, B);
  and and_1 (C, A, B);
endmodule

module HS (
  input  A,
  input  B,
  output D,
  output B_2
);

  wire not_1_out;

  xor xor_1 (D, A, B);
  not not_1 (not_1_out, A);
  and and_1 (B_2, not_1_out, B);
endmodule

module FA (
  input  A,
  input  B,
  input  CIN,
  output S,
  output COUT
);

  wire ha_1_c, ha_1_s, ha_2_c;

  HA ha_1 (.A(A), .B(B), .S(ha_1_s), .C(ha_1_c));
  or or_1 (COUT, ha_1_c, ha_2_c);
  HA ha_2 (.A(ha_1_s), .B(CIN), .S(S), .C(ha_2_c));
endmodule

module FS (
  input  A,
  input  B,
  input  BIN,
  output D,
  output BOUT
);

  wire hs_1_b_2, hs_1_d, hs_2_b_2;

  HS hs_1 (.A(A), .B(B), .D(hs_1_d), .B_2(hs_1_b_2));
  HS hs_2 (.A(hs_1_d), .B(BIN), .D(D), .B_2(hs_2_b_2));
  or or_1 (BOUT, hs_2_b_2, hs_1_b_2);
endmodule

module PA (
  input  [3:0] A,
  input  [3:0] B,
  output COUT,
  output [3:0] S
);

  wire fa_2_cout, fa_3_cout, fa_4_cout;

  FA fa_1 (.A(A[3]), .B(B[3]), .CIN(fa_2_cout), .COUT(COUT), .S(S[3]));
  FA fa_2 (.A(A[2]), .B(B[2]), .CIN(fa_3_cout), .COUT(fa_2_cout), .S(S[2]));
  FA fa_3 (.A(A[1]), .B(B[1]), .CIN(fa_4_cout), .COUT(fa_3_cout), .S(S[1]));
  FA fa_4 (.A(A[0]), .B(B[0]), .CIN(1'b0), .COUT(fa_4_cout), .S(S[0]));
endmodule

module FSusingFA (
  input  A,
  input  B,
  input  CIN,
  output S,
  output COUT
);

  wire and_1_out, and_2_out, not_1_out, xor_1_out, xor_2_out;

  not not_1 (not_1_out, A);
  xor xor_1 (xor_1_out, not_1_out, B);
  xor xor_2 (xor_2_out, xor_1_out, CIN);
  and and_1 (and_1_out, xor_1_out, CIN);
  and and_2 (and_2_out, B, not_1_out);
  not not_2 (S, xor_2_out);
  or or_1 (COUT, and_1_out, and_2_out);
endmodule

module FSusingHA (
  input  in_1,
  input  in_2,
  input  in_3,
  output out_4,
  output out_5
);

  wire ha_1_c, ha_1_s, ha_2_c, ha_2_s, not_1_out;

  not not_1 (not_1_out, in_1);
  HA ha_1 (.A(not_1_out), .B(in_2), .S(ha_1_s), .C(ha_1_c));
  HA ha_2 (.A(ha_1_s), .B(in_3), .S(ha_2_s), .C(ha_2_c));
  not not_2 (out_4, ha_2_s);
  or or_1 (out_5, ha_2_c, ha_1_c);
endmodule
