// Logisim project 09.circ as structural Verilog
module _2BITCOM (
  input  A1,
  input  A0,
  input  B1,
  input  B0,
  output GT,
  output LT,
  output EQ
);

  wire and_1_out, and_2_out, and_3_out, and_4_out, not_1_out, not_2_out, not_3_out, not_4_out, xnor_1_out,
       xnor_2_out, xnor_3_out, xnor_4_out;

  not not_1 (not_1_out, B1);
  not not_2 (not_2_out, B0);
  xnor xnor_1 (xnor_1_out, A1, B1);
  not not_3 (not_3_out, A1);
  not not_4 (not_4_out, A0);
  xnor xnor_2 (xnor_2_out, A1, B1);
  xnor xnor_3 (xnor_3_out, A0, B0);
  xnor xnor_4 (xnor_4_out, A1, B1);
  and and_1 (and_1_out, A1, not_1_out);
  and and_2 (and_2_out, A0, not_2_out, xnor_1_out);
  and and_3 (and_3_out, not_3_out, B1);
  and and_4 (and_4_out, not_4_out, B0, xnor_2_out);
  and and_5 (EQ, xnor_3_out, xnor_4_out);
  or or_1 (GT, and_1_out, and_2_out);
  or or_2 (LT, and_3_out, and_4_out);
endmodule
