// Logisim project 10.circ as structural Verilog
module SR (
  input  in_1,
  input  in_2,
  output out_3,
  output out_4
);

  wire clock_1_out, nand_1_out, nand_2_out;

  Clock clock_1 (.out(clock_1_out));
  nand nand_1 (nand_1_out, in_1, clock_1_out);
  nand nand_2 (nand_2_out, clock_1_out, in_2);
  nand nand_3 (out_3, nand_1_out, out_4);
  nand nand_4 (out_4, out_3, nand_2_out);
endmodule

module D (
  input  in_1,
  output out_2,
  output out_3
);

  wire clock_1_out, nand_1_out, nand_2_out, not_1_out;

  Clock clock_1 (.out(clock_1_out));
  not not_1 (not_1_out, in_1);
  nand nand_1 (nand_1_out, in_1, clock_1_out);
  nand nand_2 (nand_2_out, clock_1_out, not_1_out);
  nand nand_3 (out_2, nand_1_out, out_3);
  nand nand_4 (out_3, out_2, nand_2_out);
endmodule

module JK (
  input  in_1,
  input  in_2,
  input  in_3,
  input  in_4,
  output out_5,
  output out_6,
  output out_7,
  output out_8
);

  wire and_1_out, and_2_out, clock_1_out, clock_2_out, nand_1_out, nand_2_out;

  Clock clock_1 (.out(clock_1_out));
  Clock clock_2 (.out(clock_2_out));
  nand nand_1 (nand_1_out, out_6, in_1, clock_1_out);
  nand nand_2 (nand_2_out, clock_1_out, in_2, out_5);
  and and_1 (and_1_out, out_7, in_3, clock_2_out);
  and and_2 (and_2_out, clock_2_out, in_4, out_8);
  nand nand_3 (out_5, nand_1_out, out_6);
  nand nand_4 (out_6, out_5, nand_2_out);
  nor nor_1 (out_7, and_1_out, out_8);
  nor nor_2 (out_8, out_7, and_2_out);
endmodule

module T (
  input  in_1,
  output out_2,
  output out_3
);

  wire and_1_out, and_2_out, clock_1_out;

  Clock clock_1 (.out(clock_1_out));
  and and_1 (and_1_out, out_2, in_1, clock_1_out);
  and and_2 (and_2_out, clock_1_out, in_1, out_3);
  nor nor_1 (out_2, and_1_out, out_3);
  nor nor_2 (out_3, out_2, and_2_out);
endmodule
