// Logisim project 11.circ as structural Verilog
module SISO (
  input  SDI,
  output SDO
);

  wire clock_1_out, j_k_ff_1_q, j_k_ff_2_q, j_k_ff_3_q, not_1_out, not_2_out, not_3_out, not_4_out;

  Clock clock_1 (.out(clock_1_out));
  J_K_Flip_Flop j_k_ff_1 (.J(SDI), .clk(clock_1_out), .K(not_1_out), .Q(j_k_ff_1_q));  // open: Qn, preset, en, reset
  not not_1 (not_1_out, SDI);
  not not_2 (not_2_out, j_k_ff_1_q);
  J_K_Flip_Flop j_k_ff_2 (
    .J(j_k_ff_1_q), .clk(clock_1_out), .K(not_2_out), .Q(j_k_ff_2_q));  // open: Qn, preset, en, reset
  not not_3 (not_3_out, j_k_ff_2_q);
  J_K_Flip_Flop j_k_ff_3 (
    .J(j_k_ff_2_q), .clk(clock_1_out), .K(not_3_out), .Q(j_k_ff_3_q));  // open: Qn, preset, en, reset
  J_K_Flip_Flop j_k_ff_4 (.J(j_k_ff_3_q), .clk(clock_1_out), .K(not_4_out), .Q(SDO));  // open: Qn, preset, en, reset
  not not_4 (not_4_out, j_k_ff_3_q);
endmodule

module PISO (
  input  in_1,
  input  [3:0] in_2,
  output [3:0] out_3
);

  wire and_1_out, and_2_out, and_3_out, and_4_out, and_5_out, and_6_out, and_7_out, and_8_out, clock_1_out,
       not_1_out, not_2_out, not_3_out, not_4_out, not_5_out, or_1_out, or_2_out, or_3_out, or_4_out;

  not not_1 (not_1_out, in_1);
  and and_1 (and_1_out, 1'b0, not_1_out);
  and and_2 (and_2_out, in_2[0], in_1);
  and and_3 (and_3_out, out_3[0], not_1_out);
  and and_4 (and_4_out, in_2[1], in_1);
  and and_5 (and_5_out, out_3[1], not_1_out);
  and and_6 (and_6_out, in_2[2], in_1);
  and and_7 (and_7_out, out_3[2], not_1_out);
  and and_8 (and_8_out, in_2[3], in_1);
  or or_1 (or_1_out, and_1_out, and_2_out);
  not not_2 (not_2_out, or_1_out);
  or or_2 (or_2_out, and_3_out, and_4_out);
  not not_3 (not_3_out, or_2_out);
  or or_3 (or_3_out, and_5_out, and_6_out);
  not not_4 (not_4_out, or_3_out);
  or or_4 (or_4_out, and_7_out, and_8_out);
  not not_5 (not_5_out, or_4_out);
  Clock clock_1 (.out(clock_1_out));
  J_K_Flip_Flop j_k_ff_1 (.J(or_1_out), .clk(clock_1_out), .K(not_2_out), .Q(out_3[0]));  // open: Qn, preset, en, reset
  J_K_Flip_Flop j_k_ff_2 (.J(or_2_out), .clk(clock_1_out), .K(not_3_out), .Q(out_3[1]));  // open: Qn, preset, en, reset
  J_K_Flip_Flop j_k_ff_3 (.J(or_3_out), .clk(clock_1_out), .K(not_4_out), .Q(out_3[2]));  // open: Qn, preset, en, reset
  J_K_Flip_Flop j_k_ff_4 (.J(or_4_out), .clk(clock_1_out), .K(not_5_out), .Q(out_3[3]));  // open: Qn, preset, en, reset
endmodule

module PIPO (
  input  [3:0] in_1,
  output [3:0] out_2
);

  wire clock_1_out, not_1_out, not_2_out, not_3_out, not_4_out;

  Clock clock_1 (.out(clock_1_out));
  J_K_Flip_Flop j_k_ff_1 (.J(in_1[0]), .clk(clock_1_out), .K(not_1_out), .Q(out_2[0]));  // open: Qn, preset, en, reset
  not not_1 (not_1_out, in_1[0]);
  not not_2 (not_2_out, in_1[1]);
  J_K_Flip_Flop j_k_ff_2 (.J(in_1[1]), .clk(clock_1_out), .K(not_2_out), .Q(out_2[1]));  // open: Qn, preset, en, reset
  not not_3 (not_3_out, in_1[2]);
  J_K_Flip_Flop j_k_ff_3 (.J(in_1[2]), .clk(clock_1_out), .K(not_3_out), .Q(out_2[2]));  // open: Qn, preset, en, reset
  J_K_Flip_Flop j_k_ff_4 (.J(in_1[3]), .clk(clock_1_out), .K(not_4_out), .Q(out_2[3]));  // open: Qn, preset, en, reset
  not not_4 (not_4_out, in_1[3]);
endmodule

module SIPO (
  input  SDI,
  output [3:0] out_2
);

  wire clock_1_out, not_1_out, not_2_out, not_3_out, not_4_out;

  Clock clock_1 (.out(clock_1_out));
  J_K_Flip_Flop j_k_ff_1 (.J(SDI), .clk(clock_1_out), .K(not_1_out), .Q(out_2[0]));  // open: Qn, preset, en, reset
  not not_1 (not_1_out, SDI);
  not not_2 (not_2_out, out_2[0]);
  J_K_Flip_Flop j_k_ff_2 (.J(out_2[0]), .clk(clock_1_out), .K(not_2_out), .Q(out_2[1]));  // open: Qn, preset, en, reset
  not not_3 (not_3_out, out_2[1]);
  J_K_Flip_Flop j_k_ff_3 (.J(out_2[1]), .clk(clock_1_out), .K(not_3_out), .Q(out_2[2]));  // open: Qn, preset, en, reset
  J_K_Flip_Flop j_k_ff_4 (.J(out_2[2]), .clk(clock_1_out), .K(not_4_out), .Q(out_2[3]));  // open: Qn, preset, en, reset
  not not_4 (not_4_out, out_2[2]);
endmodule
