// Logisim project 12.circ as structural Verilog
module BINASUP (
  output [3:0] out_1
);

  wire clock_1_out, not_1_out, not_2_out, not_3_out, not_4_out;

  Clock clock_1 (.out(clock_1_out));
  not not_1 (not_1_out, clock_1_out);
  J_K_Flip_Flop j_k_ff_1 (.J(1'b1), .clk(not_1_out), .K(1'b1), .Q(out_1[0]));  // open: Qn, preset, en, reset
  not not_2 (not_2_out, out_1[0]);
  J_K_Flip_Flop j_k_ff_2 (.J(1'b1), .clk(not_2_out), .K(1'b1), .Q(out_1[1]));  // open: Qn, preset, en, reset
  J_K_Flip_Flop j_k_ff_3 (.J(1'b1), .clk(not_3_out), .K(1'b1), .Q(out_1[2]));  // open: Qn, preset, en, reset
  not not_3 (not_3_out, out_1[1]);
  J_K_Flip_Flop j_k_ff_4 (.J(1'b1), .clk(not_4_out), .K(1'b1), .Q(out_1[3]));  // open: Qn, preset, en, reset
  not not_4 (not_4_out, out_1[2]);
endmodule

module BINASDOWN (
  output [3:0] out_1
);

  wire clock_1_out, j_k_ff_1_qn, j_k_ff_2_qn, j_k_ff_3_qn, not_1_out, not_2_out, not_3_out, not_4_out;

  Clock clock_1 (.out(clock_1_out));
  not not_1 (not_1_out, clock_1_out);
  J_K_Flip_Flop j_k_ff_1 (
    .J(1'b1), .clk(not_1_out), .K(1'b1), .Q(out_1[0]), .Qn(j_k_ff_1_qn));  // open: preset, en, reset
  not not_2 (not_2_out, j_k_ff_1_qn);
  J_K_Flip_Flop j_k_ff_2 (
    .J(1'b1), .clk(not_2_out), .K(1'b1), .Q(out_1[1]), .Qn(j_k_ff_2_qn));  // open: preset, en, reset
  J_K_Flip_Flop j_k_ff_3 (
    .J(1'b1), .clk(not_3_out), .K(1'b1), .Q(out_1[2]), .Qn(j_k_ff_3_qn));  // open: preset, en, reset
  not not_3 (not_3_out, j_k_ff_2_qn);
  J_K_Flip_Flop j_k_ff_4 (.J(1'b1), .clk(not_4_out), .K(1'b1), .Q(out_1[3]));  // open: Qn, preset, en, reset
  not not_4 (not_4_out, j_k_ff_3_qn);
endmodule

module BINSYUP (
  input  in_1,
  output [3:0] out_2
);

  wire and_1_out, and_2_out, and_3_out, clock_1_out;

  and and_1 (and_1_out, in_1, out_2[0]);
  and and_2 (and_2_out, and_1_out, out_2[1]);
  and and_3 (and_3_out, and_2_out, out_2[2]);
  Clock clock_1 (.out(clock_1_out));
  J_K_Flip_Flop j_k_ff_1 (.J(in_1), .clk(clock_1_out), .K(in_1), .Q(out_2[0]));  // open: Qn, preset, en, reset
  J_K_Flip_Flop j_k_ff_2 (
    .J(and_1_out), .clk(clock_1_out), .K(and_1_out), .Q(out_2[1]));  // open: Qn, preset, en, reset
  J_K_Flip_Flop j_k_ff_3 (
    .J(and_2_out), .clk(clock_1_out), .K(and_2_out), .Q(out_2[2]));  // open: Qn, preset, en, reset
  J_K_Flip_Flop j_k_ff_4 (
    .J(and_3_out), .clk(clock_1_out), .K(and_3_out), .Q(out_2[3]));  // open: Qn, preset, en, reset
endmodule

module BINSYDOWN (
  input  in_1,
  output [3:0] out_2
);

  wire and_1_out, and_2_out, and_3_out, clock_1_out, j_k_ff_1_qn, j_k_ff_2_qn, j_k_ff_3_qn;

  and and_1 (and_1_out, in_1, j_k_ff_1_qn);
  and and_2 (and_2_out, and_1_out, j_k_ff_2_qn);
  and and_3 (and_3_out, and_2_out, j_k_ff_3_qn);
  Clock clock_1 (.out(clock_1_out));
  J_K_Flip_Flop j_k_ff_1 (
    .J(in_1), .clk(clock_1_out), .K(in_1), .Q(out_2[0]), .Qn(j_k_ff_1_qn));  // open: preset, en, reset
  J_K_Flip_Flop j_k_ff_2 (
    .J(and_1_out), .clk(clock_1_out), .K(and_1_out), .Q(out_2[1]), .Qn(j_k_ff_2_qn));  // open: preset, en, reset
  J_K_Flip_Flop j_k_ff_3 (
    .J(and_2_out), .clk(clock_1_out), .K(and_2_out), .Q(out_2[2]), .Qn(j_k_ff_3_qn));  // open: preset, en, reset
  J_K_Flip_Flop j_k_ff_4 (
    .J(and_3_out), .clk(clock_1_out), .K(and_3_out), .Q(out_2[3]));  // open: Qn, preset, en, reset
endmodule

module RING (
  output [3:0] out_1
);

  wire clock_1_out, not_1_out, not_2_out, not_3_out, not_4_out;

  Clock clock_1 (.out(clock_1_out));
  not not_1 (not_1_out, out_1[0]);
  J_K_Flip_Flop j_k_ff_1 (.J(out_1[0]), .clk(clock_1_out), .K(not_1_out), .Q(out_1[3]));  // open: Qn, preset, en, reset
  not not_2 (not_2_out, out_1[3]);
  J_K_Flip_Flop j_k_ff_2 (.J(out_1[3]), .clk(clock_1_out), .K(not_2_out), .Q(out_1[2]));  // open: Qn, preset, en, reset
  not not_3 (not_3_out, out_1[2]);
  J_K_Flip_Flop j_k_ff_3 (.J(out_1[2]), .clk(clock_1_out), .K(not_3_out), .Q(out_1[1]));  // open: Qn, preset, en, reset
  not not_4 (not_4_out, out_1[1]);
  J_K_Flip_Flop j_k_ff_4 (.J(out_1[1]), .clk(clock_1_out), .K(not_4_out), .Q(out_1[0]));  // open: Qn, preset, en, reset
endmodule

module JOHNSON (
  output [3:0] out_1
);

  wire clock_1_out, not_1_out, not_2_out, not_3_out, not_4_out, not_5_out;

  Clock clock_1 (.out(clock_1_out));
  not not_1 (not_1_out, not_3_out);
  J_K_Flip_Flop j_k_ff_1 (
    .J(not_3_out), .clk(clock_1_out), .K(not_1_out), .Q(out_1[3]));  // open: Qn, preset, en, reset
  not not_2 (not_2_out, out_1[3]);
  not not_3 (not_3_out, out_1[0]);
  J_K_Flip_Flop j_k_ff_2 (.J(out_1[3]), .clk(clock_1_out), .K(not_2_out), .Q(out_1[2]));  // open: Qn, preset, en, reset
  not not_4 (not_4_out, out_1[2]);
  J_K_Flip_Flop j_k_ff_3 (.J(out_1[2]), .clk(clock_1_out), .K(not_4_out), .Q(out_1[1]));  // open: Qn, preset, en, reset
  not not_5 (not_5_out, out_1[1]);
  J_K_Flip_Flop j_k_ff_4 (.J(out_1[1]), .clk(clock_1_out), .K(not_5_out), .Q(out_1[0]));  // open: Qn, preset, en, reset
endmodule
