// Logisim project ADDERS.circ as structural Verilog: 2 circuits, main circuit HA
module HA (
  input  A,
  input  B,
  output S,
  output C
);

  xor xor_1 (S, A, B);
  and and_1 (C, A, B);
endmodule

module FA (
  input  A,
  input  B,
  input  CIN,
  output S,
  output COUT
);

  HA ha_1 ();  // open: A, B, S, C
  HA ha_2 ();  // open: A, B, S, C
endmodule
