// Logisim project XOR_GATE.circ as structural Verilog: 3 circuits, main circuit main
module main (
  input  a,
  input  b,
  input  c,
  input  d,
  output x
);

  wire and_1_out, and_2_out, and_3_out, not_1_out, or_1_out;

  and and_1 (and_1_out, c, d);
  or or_1 (or_1_out, and_1_out, b);
  not not_1 (not_1_out, c);
  and and_2 (and_2_out, a, or_1_out);
  and and_3 (and_3_out, b, not_1_out);
  or or_2 (x, and_2_out, and_3_out);
endmodule

module XOR (
  input  a,
  input  b,
  output x
);

  wire and_1_out, and_2_out, not_1_out, not_2_out;

  not not_1 (not_1_out, a);
  not not_2 (not_2_out, b);
  and and_1 (and_1_out, not_1_out, b);
  or or_1 (x, and_1_out, and_2_out);
  and and_2 (and_2_out, a, not_2_out);
endmodule

module practice (
  input  a,
  input  b,
  input  c,
  input  d,
  input  e,
  output x
);

  wire nand_1_out, nand_2_out, nand_3_out, nand_4_out, nand_5_out, nand_6_out, nand_7_out;

  nand nand_1 (nand_1_out, a, a);
  nand nand_2 (nand_2_out, b, b);
  nand nand_3 (nand_3_out, c, c);
  nand nand_4 (nand_4_out, d, d);
  nand nand_5 (nand_5_out, nand_1_out, nand_2_out);
  nand nand_6 (nand_6_out, nand_3_out, nand_4_out);
  nand nand_7 (nand_7_out, nand_5_out, nand_6_out, e);
  nand nand_8 (x, nand_7_out, nand_7_out);
endmodule
