// Logisim project LAB_01.circ as structural Verilog
module SIM_01 (
  input  A,
  input  B,
  output Y
);

  wire and_1_out, and_2_out, not_1_out, not_2_out;

  not not_1 (not_1_out, B);
  not not_2 (not_2_out, A);
  and and_1 (and_1_out, A, not_1_out);
  and and_2 (and_2_out, not_2_out, B);
  or or_1 (Y, and_1_out, and_2_out);

  // Notes on the sheet:
  //   Y = A~B+~AB
endmodule

module SIM_02 (
  input  B,
  input  C,
  output W
);

  wire and_1_out, and_2_out, not_1_out;

  not not_1 (not_1_out, B);
  and and_1 (and_1_out, B, C);
  or or_1 (W, and_1_out, and_2_out);
  and and_2 (and_2_out, not_1_out, C);

  // Notes on the sheet:
  //   W = BC+~BC
endmodule

module SIM_03 (
  input  A,
  input  B,
  input  C,
  output O
);

  wire and_1_out, and_2_out, and_3_out, not_1_out, not_2_out;

  not not_1 (not_1_out, A);
  and and_1 (and_1_out, not_1_out, B, C);
  and and_2 (and_2_out, A, not_2_out, C);
  not not_2 (not_2_out, B);
  and and_3 (and_3_out, A, B, C);
  or or_1 (O, and_1_out, and_2_out, and_3_out);

  // Notes on the sheet:
  //   O = ~ABC + A~BC + ABC
endmodule

module SIM_04 (
  input  A,
  input  B,
  input  C,
  input  D,
  output X
);

  wire and_1_out, and_2_out, and_3_out, and_4_out, not_1_out, not_2_out, not_3_out, not_4_out, not_5_out,
       not_6_out, not_7_out;

  not not_1 (not_1_out, A);
  not not_2 (not_2_out, A);
  not not_3 (not_3_out, C);
  not not_4 (not_4_out, A);
  not not_5 (not_5_out, A);
  not not_6 (not_6_out, C);
  not not_7 (not_7_out, D);
  and and_1 (and_1_out, not_1_out, B);
  and and_2 (and_2_out, not_2_out, B, not_3_out);
  and and_3 (and_3_out, not_4_out, B, C, D);
  and and_4 (and_4_out, not_5_out, B, not_6_out, not_7_out);
  or or_1 (X, and_1_out, and_2_out, and_3_out, and_4_out);

  // Notes on the sheet:
  //   X = ~AB + ~AB~C + ~ABCD + ~AB~C~D
endmodule

module SIM_05 (
  input  W,
  input  X,
  input  Y,
  input  Z,
  output F
);

  wire and_1_out, and_2_out, and_3_out, and_4_out, not_1_out, not_2_out, not_3_out, not_4_out;

  not not_1 (not_1_out, W);
  not not_2 (not_2_out, W);
  not not_3 (not_3_out, Z);
  not not_4 (not_4_out, Z);
  and and_1 (and_1_out, not_1_out, X, Y, Z);
  and and_2 (and_2_out, not_2_out, X, Y, not_3_out);
  and and_3 (and_3_out, W, X, Y, Z);
  and and_4 (and_4_out, W, X, Y, not_4_out);
  or or_1 (F, and_1_out, and_2_out, and_3_out, and_4_out);

  // Notes on the sheet:
  //   F = ~WXYZ + ~WXY~Z + WXYZ + WXY~Z
endmodule
