// Logisim project LAB_02.circ as structural Verilog
module SIM_01 (
  input  A,
  input  B,
  input  C,
  input  D,
  output F
);

  wire nand_1_out, nand_2_out;

  nand nand_1 (nand_1_out, C, D);
  nand nand_2 (nand_2_out, A, B);
  nand nand_3 (F, nand_1_out, nand_2_out);

  // Notes on the sheet:
  //   F = AB + CD
endmodule

module SIM_02 (
  input  X,
  input  Y,
  input  Z,
  output F
);

  wire nand_1_out, nand_2_out, nand_3_out, nand_4_out, nand_5_out;

  nand nand_1 (nand_1_out, Y, Y);
  nand nand_2 (nand_2_out, X, X);
  nand nand_3 (nand_3_out, X, nand_1_out);
  nand nand_4 (nand_4_out, nand_2_out, Y);
  nand nand_5 (nand_5_out, Z, Z);
  nand nand_6 (F, nand_3_out, nand_4_out, nand_5_out);

  // Notes on the sheet:
  //   F = X~Y + ~XY + Z
endmodule

module SIM_03 (
  input  A,
  input  B,
  input  C,
  input  D,
  output F
);

  wire nand_1_out, nand_2_out, nand_3_out, nand_4_out, nand_5_out, nand_6_out;

  nand nand_1 (nand_1_out, C, D);
  nand nand_2 (nand_2_out, B, B);
  nand nand_3 (nand_3_out, nand_1_out, nand_2_out);
  nand nand_4 (nand_4_out, C, C);
  nand nand_5 (nand_5_out, A, nand_3_out);
  nand nand_6 (nand_6_out, B, nand_4_out);
  nand nand_7 (F, nand_5_out, nand_6_out);

  // Notes on the sheet:
  //   F = A(CD + B) + BC
endmodule

module SIM_04 (
  input  A,
  input  B,
  input  C,
  output F
);

  wire nand_1_out, nand_2_out, nand_3_out;

  nand nand_1 (nand_1_out, A, B);
  nand nand_2 (nand_2_out, B, C);
  nand nand_3 (nand_3_out, A, C);
  nand nand_4 (F, nand_1_out, nand_2_out, nand_3_out);

  // Notes on the sheet:
  //   F = AB + BC + AC
endmodule

module SIM_05 (
  input  A,
  input  B,
  input  C,
  input  D,
  input  E,
  output F
);

  wire nand_1_out, nand_2_out, nand_3_out, nand_4_out, nand_5_out, nand_6_out, nand_7_out;

  nand nand_1 (nand_1_out, A, A);
  nand nand_2 (nand_2_out, B, B);
  nand nand_3 (nand_3_out, C, C);
  nand nand_4 (nand_4_out, D, D);
  nand nand_5 (nand_5_out, nand_1_out, nand_2_out);
  nand nand_6 (nand_6_out, nand_3_out, nand_4_out);
  nand nand_7 (nand_7_out, nand_5_out, nand_6_out, E);
  nand nand_8 (F, nand_7_out, nand_7_out);
endmodule

module SIM_06 (
  input  A,
  input  B,
  input  C,
  output F
);

  wire nand_1_out, nand_2_out, nand_3_out, nand_4_out, nand_5_out, nand_6_out;

  nand nand_1 (nand_1_out, A, A);
  nand nand_2 (nand_2_out, B, B);
  nand nand_3 (nand_3_out, C, C);
  nand nand_4 (nand_4_out, nand_1_out, nand_2_out, nand_3_out);
  nand nand_5 (nand_5_out, A, B, C);
  nand nand_6 (nand_6_out, nand_4_out, nand_5_out);
  nand nand_7 (F, nand_6_out, nand_6_out);
endmodule
