// Logisim project LAB_03.circ as structural Verilog
module CKT_01 (
  input  A,
  input  B,
  input  C,
  output F
);


  assign F = C;
endmodule

module CKT_02 (
  input  A,
  input  B,
  input  C,
  input  D,
  output F
);

  wire and_1_out, and_2_out, and_3_out, and_4_out, not_1_out, not_2_out, not_3_out;

  not not_1 (not_1_out, A);
  not not_2 (not_2_out, B);
  and and_1 (and_1_out, not_1_out, not_2_out, not_3_out);
  not not_3 (not_3_out, D);
  and and_2 (and_2_out, C, D);
  and and_3 (and_3_out, A, B, D);
  and and_4 (and_4_out, A, B, C);
  or or_1 (F, and_1_out, and_2_out, and_3_out, and_4_out);
endmodule

module CKT_03 (
  input  A,
  input  B,
  input  C,
  output F
);

  wire nand_1_out, nand_2_out;

  nand nand_1 (nand_1_out, B, B);
  nand nand_2 (nand_2_out, A, A);
  nand nand_3 (F, nand_1_out, nand_2_out);
endmodule

module CKT_04 (
  input  A,
  input  B,
  input  C,
  input  D,
  output F
);

  wire nand_1_out, nand_2_out, nand_3_out, nand_4_out, nand_5_out, nand_6_out, nand_7_out;

  nand nand_1 (nand_1_out, B, B);
  nand nand_2 (nand_2_out, D, D);
  nand nand_3 (nand_3_out, A, A);
  nand nand_4 (nand_4_out, C, C);
  nand nand_5 (nand_5_out, nand_1_out, nand_2_out);
  nand nand_6 (nand_6_out, nand_3_out, B, D);
  nand nand_7 (nand_7_out, A, B, nand_4_out);
  nand nand_8 (F, nand_5_out, nand_6_out, nand_7_out);
endmodule

module CKT_05 (
  input  A,
  input  B,
  input  C,
  input  D,
  output F
);

  wire not_1_out, not_2_out, not_3_out, or_1_out, or_2_out;

  or or_1 (or_1_out, A, not_1_out);
  not not_1 (not_1_out, D);
  not not_2 (not_2_out, B);
  or or_2 (or_2_out, not_2_out, not_3_out);
  not not_3 (not_3_out, D);
  and and_1 (F, or_1_out, or_2_out);
endmodule

module CKT_06 (
  input  A,
  input  B,
  input  C,
  input  D,
  output F
);

  wire not_1_out, not_2_out, not_3_out, not_4_out, not_5_out, or_1_out, or_2_out, or_3_out;

  or or_1 (or_1_out, B, not_1_out);
  not not_1 (not_1_out, D);
  not not_2 (not_2_out, B);
  or or_2 (or_2_out, not_2_out, not_3_out, D);
  not not_3 (not_3_out, C);
  not not_4 (not_4_out, A);
  or or_3 (or_3_out, not_4_out, not_5_out, D);
  not not_5 (not_5_out, B);
  and and_1 (F, or_1_out, or_2_out, or_3_out);
endmodule

module CKT_07 (
  input  A,
  input  B,
  input  C,
  input  D,
  output F
);

  wire not_1_out, not_2_out, not_3_out, not_4_out, not_5_out, not_6_out, or_1_out, or_2_out, or_3_out;

  not not_1 (not_1_out, B);
  or or_1 (or_1_out, not_1_out, C, not_2_out);
  not not_2 (not_2_out, D);
  not not_3 (not_3_out, A);
  or or_2 (or_2_out, not_3_out, not_4_out);
  not not_4 (not_4_out, D);
  not not_5 (not_5_out, A);
  or or_3 (or_3_out, not_5_out, not_6_out);
  not not_6 (not_6_out, B);
  and and_1 (F, or_1_out, or_2_out, or_3_out);
endmodule
