// Logisim project LAB_04.circ as structural Verilog
module BCD2GRAY (
  input  B0,
  input  B1,
  input  B2,
  input  B3,
  output D0,
  output D1,
  output D2,
  output D3
);

  wire nand_1_out, nand_2_out, nand_3_out, nand_4_out, nand_5_out, nand_6_out, nand_7_out, nand_8_out,
       nand_9_out, nand_10_out;

  nand nand_1 (nand_1_out, B2, B2);
  nand nand_2 (nand_2_out, B3, B3);
  nand nand_3 (nand_3_out, B1, B1);
  nand nand_4 (nand_4_out, B2, B2);
  nand nand_5 (nand_5_out, B1, B1);
  nand nand_6 (nand_6_out, B0, B0);
  nand nand_7 (nand_7_out, nand_1_out, B3);
  nand nand_8 (nand_8_out, B2, nand_2_out);
  nand nand_9 (nand_9_out, nand_3_out, B2);
  nand nand_10 (nand_10_out, B1, nand_4_out);
  nand nand_11 (D2, nand_5_out, nand_6_out);
  nand nand_12 (D0, nand_7_out, nand_8_out);
  nand nand_13 (D1, nand_9_out, nand_10_out);

  assign D3 = B0;
endmodule

module GRAY2BCD (
  input  D3,
  input  D2,
  input  D1,
  input  D0,
  output B3,
  output B2,
  output B1,
  output B0
);

  wire and_1_out, and_2_out, and_3_out, and_4_out, and_5_out, and_6_out, and_7_out, and_8_out, and_9_out,
       and_10_out, and_11_out, and_12_out, and_13_out, and_14_out, not_1_out, not_2_out, not_3_out,
       not_4_out, not_5_out, not_6_out, not_7_out, not_8_out, not_9_out, not_10_out, not_11_out, not_12_out,
       not_13_out, not_14_out, not_15_out, not_16_out, not_17_out, not_18_out, not_19_out, not_20_out,
       not_21_out, not_22_out, not_23_out, not_24_out;

  not not_1 (not_1_out, D3);
  and and_1 (and_1_out, not_1_out, D2);
  and and_2 (and_2_out, D3, not_2_out);
  not not_2 (not_2_out, D2);
  not not_3 (not_3_out, D3);
  not not_4 (not_4_out, D2);
  and and_3 (and_3_out, not_3_out, not_4_out, D1);
  not not_5 (not_5_out, D3);
  and and_4 (and_4_out, not_5_out, D2, not_6_out);
  not not_6 (not_6_out, D1);
  and and_5 (and_5_out, D3, not_7_out, not_8_out);
  not not_7 (not_7_out, D2);
  not not_8 (not_8_out, D1);
  and and_6 (and_6_out, D3, D2, D1);
  not not_9 (not_9_out, D3);
  not not_10 (not_10_out, D2);
  not not_11 (not_11_out, D1);
  not not_12 (not_12_out, D3);
  not not_13 (not_13_out, D2);
  not not_14 (not_14_out, D0);
  not not_15 (not_15_out, D3);
  not not_16 (not_16_out, D1);
  not not_17 (not_17_out, D0);
  not not_18 (not_18_out, D3);
  not not_19 (not_19_out, D2);
  not not_20 (not_20_out, D1);
  not not_21 (not_21_out, D0);
  not not_22 (not_22_out, D2);
  not not_23 (not_23_out, D1);
  not not_24 (not_24_out, D0);
  or or_1 (B2, and_1_out, and_2_out);
  or or_2 (B1, and_3_out, and_4_out, and_5_out, and_6_out);
  and and_7 (and_7_out, not_9_out, not_10_out, not_11_out, D0);
  and and_8 (and_8_out, not_12_out, not_13_out, D1, not_14_out);
  and and_9 (and_9_out, not_15_out, D2, not_16_out, not_17_out);
  and and_10 (and_10_out, not_18_out, D2, D1, D0);
  and and_11 (and_11_out, D3, not_19_out, not_20_out, not_21_out);
  and and_12 (and_12_out, D3, not_22_out, D1, D0);
  and and_13 (and_13_out, D3, D2, not_23_out, D0);
  and and_14 (and_14_out, D3, D2, D1, not_24_out);
  or or_3 (B0, and_7_out, and_8_out, and_9_out, and_10_out, and_11_out, and_12_out, and_13_out, and_14_out);

  assign B3 = D3;
endmodule
