// Logisim project LAB_05.circ as structural Verilog
module HA (
  input  A,
  input  B,
  output S,
  output C
);

  xor xor_1 (S, A, B);
  and and_1 (C, A, B);
endmodule

module FA (
  input  A,
  input  B,
  input  CIN,
  output S,
  output COUT
);

  wire and_1_out, and_2_out, xor_1_out;

  and and_1 (and_1_out, A, B);
  xor xor_1 (xor_1_out, A, B);
  xor xor_2 (S, xor_1_out, CIN);
  and and_2 (and_2_out, CIN, xor_1_out);
  or or_1 (COUT, and_2_out, and_1_out);
endmodule

module HS (
  input  A,
  input  B,
  output D,
  output B2
);

  wire not_1_out;

  xor xor_1 (D, A, B);
  not not_1 (not_1_out, A);
  and and_1 (B2, not_1_out, B);
endmodule

module FS (
  input  A,
  input  B,
  input  BIN,
  output D,
  output BOUT
);

  wire and_1_out, and_2_out, not_1_out, not_2_out, xor_1_out;

  not not_1 (not_1_out, A);
  xor xor_1 (xor_1_out, A, B);
  and and_1 (and_1_out, B, not_1_out);
  xor xor_2 (D, xor_1_out, BIN);
  not not_2 (not_2_out, xor_1_out);
  and and_2 (and_2_out, BIN, not_2_out);
  or or_1 (BOUT, and_2_out, and_1_out);
endmodule

module ADDSUB (
  input  B1,
  input  B0,
  input  M,
  input  A1,
  input  A0,
  output COUT,
  output S1,
  output S0
);

  wire fa_2_cout, xor_1_out, xor_2_out;

  xor xor_1 (xor_1_out, B1, M);
  FA fa_1 (.A(A1), .B(xor_1_out), .CIN(fa_2_cout), .S(S1), .COUT(COUT));
  xor xor_2 (xor_2_out, B0, M);
  FA fa_2 (.A(A0), .B(xor_2_out), .CIN(M), .S(S0), .COUT(fa_2_cout));
endmodule

module FA2 (
  input  A,
  input  B,
  input  CIN,
  output S,
  output COUT
);

  wire and_1_out, and_2_out, xor_1_out;

  xor xor_1 (xor_1_out, A, B);
  xor xor_2 (S, xor_1_out, CIN);
  and and_1 (and_1_out, CIN, xor_1_out);
  and and_2 (and_2_out, A, B);
  or or_1 (COUT, and_1_out, and_2_out);
endmodule

module FA3 (
  input  A,
  input  B,
  input  CIN,
  output S,
  output COUT
);

  wire HA1_c, HA1_s, HA2_c;

  HA HA1 (.A(A), .B(B), .S(HA1_s), .C(HA1_c));
  HA HA2 (.A(HA1_s), .B(CIN), .S(S), .C(HA2_c));
  or or_1 (COUT, HA2_c, HA1_c);
endmodule
