// Logisim project LAB_06.circ as structural Verilog
module _41MUX (
  input  [3:0] in_1,
  input  [1:0] in_2,
  output out_3
);

  Multiplexer #(.select(2), .enable("false")) multiplexer_1 (
    .in0(in_1[0]), .in1(in_1[1]), .in2(in_1[2]), .in3(in_1[3]), .out(out_3), .sel(in_2));
endmodule

module _81MUX (
  input  [7:0] in_1,
  input  [2:0] in_2,
  output out_3
);

  Multiplexer #(.select(3), .enable("false")) multiplexer_1 (
    .in0(in_1[0]), .in1(in_1[1]), .in2(in_1[2]), .in3(in_1[3]), .in4(in_1[4]), .in5(in_1[5]), .in6(in_1[6]),
    .in7(in_1[7]), .out(out_3), .sel(in_2));
endmodule

module _14DEMUX (
  input  in_1,
  input  [1:0] in_2,
  output [3:0] out_3
);

  Demultiplexer #(.select(2), .enable("false")) demultiplexer_1 (
    .out0(out_3[0]), .out1(out_3[1]), .out2(out_3[2]), .out3(out_3[3]), .in(in_1), .sel(in_2));
endmodule

module _18DEMUX (
  input  in_1,
  input  [2:0] in_2,
  output [7:0] out_3
);

  Demultiplexer #(.select(3), .enable("false")) demultiplexer_1 (
    .out0(out_3[0]), .out1(out_3[1]), .out2(out_3[2]), .out3(out_3[3]), .out4(out_3[4]), .out5(out_3[5]),
    .out6(out_3[6]), .out7(out_3[7]), .in(in_1), .sel(in_2));
endmodule

module MUXSOP (
  input  D,
  input  C,
  input  B,
  input  A,
  output F
);

  wire not_1_out;

  not not_1 (not_1_out, D);
  Multiplexer #(.select(3), .enable("false")) multiplexer_1 (
    .in0(D), .in1(D), .in2(not_1_out), .in3(1'b0), .in4(1'b0), .in5(D), .in6(1'b1), .in7(1'b1), .out(F),
    .sel({A, B, C}));
endmodule
