// Logisim project LAB_07.circ as structural Verilog
module DEC2BCDENC (
  input  D9,
  input  D8,
  input  D7,
  input  D6,
  input  D5,
  input  D4,
  input  D3,
  input  D2,
  input  D1,
  input  D0,
  output B3,
  output B2,
  output B1,
  output B0
);

  or or_1 (B3, D8, D9);
  or or_2 (B2, D4, D5, D6, D7);
  or or_3 (B1, D2, D3, D6, D7);
  or or_4 (B0, D1, D3, D5, D7, D9);
endmodule

module DEMUX2DEC (
  input  S0,
  input  S1,
  output I0,
  output I1,
  output I2,
  output I3
);

  Demultiplexer #(.select(2), .enable("false")) demultiplexer_1 (
    .out0(I0), .out1(I1), .out2(I2), .out3(I3), .in(1'b1), .sel({S1, S0}));
endmodule
